// Logisim project riscv_latest.circ as structural Verilog: 5 circuits, main circuit main
module main (
);

  wire and_3_out, and_4_out, and_5_out, and_7_out, and_8_out, button_1_out, clock_1_out, comparator_1_eq,
       comparator_1_lt, comparator_2_eq, comparator_3_eq, comparator_4_eq, comparator_4_lt, comparator_5_lt,
       nor_1_out, nor_2_out, nor_3_out, nor_4_out, not_1_out, not_2_out, not_3_out, not_4_out, not_5_out,
       or_2_out, pull_resistor_1_node, pull_resistor_11_node, pull_resistor_12_node, System_reset_latch_q,
       t_ff_1_q;
  wire [0:0] pull_resistor_9_node;
  wire [2:0] instruction_decoder_1_funct3, pull_resistor_6_node;
  wire [4:0] instruction_decoder_1_rd, instruction_decoder_1_rs1, instruction_decoder_1_rs2;
  wire [5:0] instruction_decoder_1_instr_type;
  wire [6:0] and_1_out, instruction_decoder_1_funct7, instruction_decoder_1_opcode, pull_resistor_5_node;
  wire [11:0] pull_resistor_8_node;
  wire [19:0] instruction_decoder_1_imm;
  wire [31:0] adder_1_out, and_2_out, bit_extender_1_out, bit_extender_2_out, controlled_buffer_3_out,
       controlled_buffer_5_out, controlled_buffer_9_out, controlled_buffer_12_out, program_counter_1_instr,
       register_block_1_rs1, register_block_1_rs2;
  wire [33:0] program_counter_1_pc_data;

  Clock clock_1 (.out(clock_1_out));
  Pull_Resistor pull_resistor_1 (.node(pull_resistor_1_node));
  S_R_Flip_Flop System_reset_latch (
    .S(pull_resistor_1_node), .R(pull_resistor_1_node), .clk(clock_1_out), .Q(System_reset_latch_q),
    .reset(button_1_out), .preset(clock_1_out));  // open: Qn
  Button button_1 (.out(button_1_out));
  Pull_Resistor pull_resistor_2 (.node(System_reset_latch_q));
  not not_1 (not_1_out, System_reset_latch_q);
  Pull_Resistor pull_resistor_3 (.node(not_1_out));
  program_counter program_counter_1 (
    .clk(clock_1_out), .rst(not_1_out), .read_next(program_counter_1_pc_data[33]),
    .write_enable(program_counter_1_pc_data[32]), .instr(program_counter_1_instr),
    .pc_data(program_counter_1_pc_data[31:0]));
  register_block register_block_1 (
    .RS1(register_block_1_rs1), .RS2(register_block_1_rs2), .RD(controlled_buffer_12_out),
    .RS1S(instruction_decoder_1_rs1), .RST(not_1_out), .RS2S(instruction_decoder_1_rs2),
    .RDS(instruction_decoder_1_rd), .CLK(clock_1_out));
  Pull_Resistor #(.pull(1)) pull_resistor_4 (.node(register_block_1_rs1));
  or or_1 (program_counter_1_pc_data[32], and_7_out, and_4_out);
  Pull_Resistor pull_resistor_5 (.node(pull_resistor_5_node));
  Comparator #(.mode("unsigned"), .width(7)) comparator_1 (
    .a(pull_resistor_5_node), .b(and_1_out), .eq(comparator_1_eq), .lt(comparator_1_lt));  // open: gt
  assign and_1_out = instruction_decoder_1_opcode & 7'b0100000;  // AND_Gate and_1, 7 bits wide
  instruction_decoder instruction_decoder_1 (
    .instr(program_counter_1_instr), .instr_type(instruction_decoder_1_instr_type),
    .opcode(instruction_decoder_1_opcode), .imm(instruction_decoder_1_imm),
    .funct7(instruction_decoder_1_funct7), .funct3(instruction_decoder_1_funct3),
    .rd(instruction_decoder_1_rd), .rs2(instruction_decoder_1_rs2), .rs1(instruction_decoder_1_rs1));  // open: invalid
  assign program_counter_1_pc_data[31:0] = and_4_out ? and_2_out : 32'bz;  // Controlled_Buffer controlled_buffer_1
  assign and_2_out = 32'hfffffffe & controlled_buffer_9_out;  // AND_Gate and_2, 32 bits wide
  assign program_counter_1_pc_data[31:0] = and_7_out ? controlled_buffer_9_out : 32'bz;  // Controlled_Buffer controlled_buffer_2
  assign controlled_buffer_3_out = and_3_out ? program_counter_1_pc_data[31:0] : 32'bz;  // Controlled_Buffer controlled_buffer_3
  and and_3 (and_3_out, comparator_1_eq, instruction_decoder_1_instr_type[4]);
  assign controlled_buffer_3_out = nor_1_out ? register_block_1_rs1 : 32'bz;  // Controlled_Buffer controlled_buffer_4
  assign controlled_buffer_5_out = nor_2_out ? register_block_1_rs2 : 32'bz;  // Controlled_Buffer controlled_buffer_5
  not nor_1 (nor_1_out, and_3_out);  // NOR_Gate
  and and_4 (and_4_out, t_ff_1_q, and_5_out);
  nor nor_2 (nor_2_out, and_5_out, instruction_decoder_1_instr_type[4], pull_resistor_12_node, pull_resistor_11_node);
  T_Flip_Flop t_ff_1 (.T(program_counter_1_pc_data[33]), .clk(clock_1_out), .Q(t_ff_1_q));  // open: Qn, reset, preset
  Comparator #(.width(3)) comparator_2 (
    .a(instruction_decoder_1_funct3), .b(pull_resistor_6_node), .eq(comparator_2_eq));  // open: gt, lt
  Pull_Resistor pull_resistor_6 (.node(pull_resistor_6_node));
  Comparator #(.width(7)) comparator_3 (
    .a(instruction_decoder_1_opcode), .b(7'b1100111), .eq(comparator_3_eq));  // open: gt, lt
  Pull_Resistor pull_resistor_7 (.node(t_ff_1_q));
  and and_5 (and_5_out, comparator_2_eq, comparator_3_eq);
  not not_2 (not_2_out, t_ff_1_q);
  and and_6 (program_counter_1_pc_data[33], not_2_out, or_2_out);
  or or_2 (or_2_out, and_5_out, t_ff_1_q);
  and and_7 (and_7_out, t_ff_1_q, instruction_decoder_1_instr_type[5]);
  and and_8 (and_8_out, comparator_1_lt, instruction_decoder_1_instr_type[4]);
  assign controlled_buffer_5_out = and_4_out ? bit_extender_1_out : 32'bz;  // Controlled_Buffer controlled_buffer_6
  Pull_Resistor pull_resistor_8 (.node(pull_resistor_8_node));
  assign bit_extender_1_out = {{20{instruction_decoder_1_imm[11]}}, instruction_decoder_1_imm[11:0]};  // Bit_Extender bit_extender_1
  assign controlled_buffer_5_out = instruction_decoder_1_instr_type[4] ? {instruction_decoder_1_imm, pull_resistor_8_node} : 32'bz;  // Controlled_Buffer controlled_buffer_7
  assign controlled_buffer_5_out = pull_resistor_12_node ? 32'h4 : 32'bz;  // Controlled_Buffer controlled_buffer_8
  assign controlled_buffer_9_out = and_7_out ? bit_extender_2_out : 32'bz;  // Controlled_Buffer controlled_buffer_9
  assign controlled_buffer_5_out = pull_resistor_11_node ? bit_extender_2_out : 32'bz;  // Controlled_Buffer controlled_buffer_10
  Pull_Resistor pull_resistor_9 (.node(pull_resistor_9_node[0]));
  Pull_Resistor pull_resistor_10 (.node(instruction_decoder_1_instr_type[4]));
  assign bit_extender_2_out = {{11{instruction_decoder_1_imm[19]}}, {instruction_decoder_1_imm, pull_resistor_9_node[0]}};  // Bit_Extender bit_extender_2
  Comparator #(.width(32)) comparator_4 (
    .a(register_block_1_rs2), .b(register_block_1_rs1), .eq(comparator_4_eq), .lt(comparator_4_lt));  // open: gt
  Comparator #(.mode("unsigned"), .width(32)) comparator_5 (
    .a(register_block_1_rs2), .b(register_block_1_rs1), .lt(comparator_5_lt));  // open: gt, eq
  nor nor_3 (nor_3_out, program_counter_1_pc_data[33], and_7_out);
  assign controlled_buffer_9_out = nor_3_out ? adder_1_out : 32'bz;  // Controlled_Buffer controlled_buffer_11
  Adder #(.width(32)) adder_1 (
    .a(controlled_buffer_3_out), .b(controlled_buffer_5_out), .out(adder_1_out));  // open: cin, cout
  Pull_Resistor pull_resistor_11 (.node(pull_resistor_11_node));
  Pull_Resistor pull_resistor_12 (.node(pull_resistor_12_node));
  not not_3 (not_3_out, comparator_4_eq);
  assign controlled_buffer_12_out = program_counter_1_pc_data[33] ? program_counter_1_pc_data[31:0] : 32'bz;  // Controlled_Buffer controlled_buffer_12
  assign controlled_buffer_12_out = and_8_out ? {instruction_decoder_1_imm, pull_resistor_8_node} : 32'bz;  // Controlled_Buffer controlled_buffer_13
  nor nor_4 (nor_4_out, and_8_out, and_7_out, program_counter_1_pc_data[33]);
  assign controlled_buffer_12_out = nor_4_out ? controlled_buffer_9_out : 32'bz;  // Controlled_Buffer controlled_buffer_14
  not not_4 (not_4_out, comparator_4_lt);
  not not_5 (not_5_out, comparator_5_lt);

  // Notes on the sheet:
  //   4 cycles per instruction
  //   33:PC+4,32:WE,31-0:Data
  //   Write result to PC
  //   rd, rs2, rs1
  //   opcode
  //   inst_type
  //   TODO: control block instead of interspersed logic and execution resources
  //   Also need better organisation
  //   Branch instruction area
  //   Write PC+4 to rd
  //   imm20 OR imm12
  //   funct3
  //   funct7
  //   rd
endmodule

module register_block (
  input  [31:0] RD,
  input  [4:0] RS1S,
  input  CLK,
  input  [4:0] RS2S,
  input  [4:0] RDS,
  input  RST,
  output [31:0] RS1,
  output [31:0] RS2
);

  wire pull_resistor_1_node, pull_resistor_4_node, pull_resistor_5_node;
  wire [31:0] x1_q, x2_q, x3_q, x4_q, x5_q, x6_q, x7_q, x8_q, x9_q, x10_q, x11_q, x12_q, x13_q, x14_q, x15_q,
       x16_q, x17_q, x18_q, x19_q, x20_q, x21_q, x22_q, x23_q, x24_q, x25_q, x26_q, x27_q, x28_q, x29_q,
       x30_q, x31_q;
  wire [34:32] decoder_3_out0, decoder_3_out1, decoder_3_out2, decoder_3_out3, decoder_3_out4,
       decoder_3_out5, decoder_3_out6, decoder_3_out7, decoder_3_out8, decoder_3_out9, decoder_3_out10,
       decoder_3_out11, decoder_3_out12, decoder_3_out13, decoder_3_out14, decoder_3_out15, decoder_3_out16,
       decoder_3_out17, decoder_3_out18, decoder_3_out19, decoder_3_out20, decoder_3_out21, decoder_3_out22,
       decoder_3_out23, decoder_3_out24, decoder_3_out25, decoder_3_out26, decoder_3_out27, decoder_3_out28,
       decoder_3_out29, decoder_3_out30, decoder_3_out31;

  Transistor #(.\type ("n"), .width(32)) transistor_1 (.in(x7_q), .out(RS1), .gate(decoder_3_out7[32]));
  Register #(.width(32)) x7 (.D(RD), .en(decoder_3_out7[34]), .clk(CLK), .Q(x7_q), .clr(RST));
  Transistor #(.\type ("n"), .width(32)) transistor_2 (.in(x15_q), .out(RS1), .gate(decoder_3_out15[32]));
  Register #(.width(32)) x15 (.D(RD), .en(decoder_3_out15[34]), .clk(CLK), .Q(x15_q), .clr(RST));
  Transistor #(.\type ("n"), .width(32)) transistor_3 (.in(x23_q), .out(RS1), .gate(decoder_3_out23[32]));
  Register #(.width(32)) x23 (.D(RD), .en(decoder_3_out23[34]), .clk(CLK), .Q(x23_q), .clr(RST));
  Transistor #(.\type ("n"), .width(32)) transistor_4 (.in(x31_q), .out(RS1), .gate(decoder_3_out31[32]));
  Register #(.width(32)) x31 (.D(RD), .en(decoder_3_out31[34]), .clk(CLK), .Q(x31_q), .clr(RST));
  Transistor #(.\type ("n"), .width(32)) transistor_5 (.in(x6_q), .out(RS1), .gate(decoder_3_out6[32]));
  Transistor #(.\type ("n"), .width(32)) transistor_6 (.in(x7_q), .out(RS2), .gate(decoder_3_out7[33]));
  Register #(.width(32)) x6 (.D(RD), .en(decoder_3_out6[34]), .clk(CLK), .Q(x6_q), .clr(RST));
  Transistor #(.\type ("n"), .width(32)) transistor_7 (.in(x14_q), .out(RS1), .gate(decoder_3_out14[32]));
  Transistor #(.\type ("n"), .width(32)) transistor_8 (.in(x15_q), .out(RS2), .gate(decoder_3_out15[33]));
  Register #(.width(32)) x14 (.D(RD), .en(decoder_3_out14[34]), .clk(CLK), .Q(x14_q), .clr(RST));
  Transistor #(.\type ("n"), .width(32)) transistor_9 (.in(x22_q), .out(RS1), .gate(decoder_3_out22[32]));
  Transistor #(.\type ("n"), .width(32)) transistor_10 (.in(x23_q), .out(RS2), .gate(decoder_3_out23[33]));
  Register #(.width(32)) x22 (.D(RD), .en(decoder_3_out22[34]), .clk(CLK), .Q(x22_q), .clr(RST));
  Transistor #(.\type ("n"), .width(32)) transistor_11 (.in(x30_q), .out(RS1), .gate(decoder_3_out30[32]));
  Transistor #(.\type ("n"), .width(32)) transistor_12 (.in(x31_q), .out(RS2), .gate(decoder_3_out31[33]));
  Register #(.width(32)) x30 (.D(RD), .en(decoder_3_out30[34]), .clk(CLK), .Q(x30_q), .clr(RST));
  Transistor #(.\type ("n"), .width(32)) transistor_13 (.in(x5_q), .out(RS1), .gate(decoder_3_out5[32]));
  Transistor #(.\type ("n"), .width(32)) transistor_14 (.in(x6_q), .out(RS2), .gate(decoder_3_out6[33]));
  Register #(.width(32)) x5 (.D(RD), .en(decoder_3_out5[34]), .clk(CLK), .Q(x5_q), .clr(RST));
  Transistor #(.\type ("n"), .width(32)) transistor_15 (.in(x13_q), .out(RS1), .gate(decoder_3_out13[32]));
  Transistor #(.\type ("n"), .width(32)) transistor_16 (.in(x14_q), .out(RS2), .gate(decoder_3_out14[33]));
  Register #(.width(32)) x13 (.D(RD), .en(decoder_3_out13[34]), .clk(CLK), .Q(x13_q), .clr(RST));
  Transistor #(.\type ("n"), .width(32)) transistor_17 (.in(x21_q), .out(RS1), .gate(decoder_3_out21[32]));
  Transistor #(.\type ("n"), .width(32)) transistor_18 (.in(x22_q), .out(RS2), .gate(decoder_3_out22[33]));
  Register #(.width(32)) x21 (.D(RD), .en(decoder_3_out21[34]), .clk(CLK), .Q(x21_q), .clr(RST));
  Transistor #(.\type ("n"), .width(32)) transistor_19 (.in(x29_q), .out(RS1), .gate(decoder_3_out29[32]));
  Transistor #(.\type ("n"), .width(32)) transistor_20 (.in(x30_q), .out(RS2), .gate(decoder_3_out30[33]));
  Register #(.width(32)) x29 (.D(RD), .en(decoder_3_out29[34]), .clk(CLK), .Q(x29_q), .clr(RST));
  Transistor #(.\type ("n"), .width(32)) transistor_21 (.in(x4_q), .out(RS1), .gate(decoder_3_out4[32]));
  Transistor #(.\type ("n"), .width(32)) transistor_22 (.in(x5_q), .out(RS2), .gate(decoder_3_out5[33]));
  Register #(.width(32)) x4 (.D(RD), .en(decoder_3_out4[34]), .clk(CLK), .Q(x4_q), .clr(RST));
  Transistor #(.\type ("n"), .width(32)) transistor_23 (.in(x12_q), .out(RS1), .gate(decoder_3_out12[32]));
  Transistor #(.\type ("n"), .width(32)) transistor_24 (.in(x13_q), .out(RS2), .gate(decoder_3_out13[33]));
  Register #(.width(32)) x12 (.D(RD), .en(decoder_3_out12[34]), .clk(CLK), .Q(x12_q), .clr(RST));
  Transistor #(.\type ("n"), .width(32)) transistor_25 (.in(x20_q), .out(RS1), .gate(decoder_3_out20[32]));
  Transistor #(.\type ("n"), .width(32)) transistor_26 (.in(x21_q), .out(RS2), .gate(decoder_3_out21[33]));
  Register #(.width(32)) x20 (.D(RD), .en(decoder_3_out20[34]), .clk(CLK), .Q(x20_q), .clr(RST));
  Transistor #(.\type ("n"), .width(32)) transistor_27 (.in(x28_q), .out(RS1), .gate(decoder_3_out28[32]));
  Transistor #(.\type ("n"), .width(32)) transistor_28 (.in(x29_q), .out(RS2), .gate(decoder_3_out29[33]));
  Register #(.width(32)) x28 (.D(RD), .en(decoder_3_out28[34]), .clk(CLK), .Q(x28_q), .clr(RST));
  Transistor #(.\type ("n"), .width(32)) transistor_29 (.in(x3_q), .out(RS1), .gate(decoder_3_out3[32]));
  Transistor #(.\type ("n"), .width(32)) transistor_30 (.in(x4_q), .out(RS2), .gate(decoder_3_out4[33]));
  Register #(.width(32)) x3 (.D(RD), .en(decoder_3_out3[34]), .clk(CLK), .Q(x3_q), .clr(RST));
  Transistor #(.\type ("n"), .width(32)) transistor_31 (.in(x11_q), .out(RS1), .gate(decoder_3_out11[32]));
  Transistor #(.\type ("n"), .width(32)) transistor_32 (.in(x12_q), .out(RS2), .gate(decoder_3_out12[33]));
  Register #(.width(32)) x11 (.D(RD), .en(decoder_3_out11[34]), .clk(CLK), .Q(x11_q), .clr(RST));
  Transistor #(.\type ("n"), .width(32)) transistor_33 (.in(x19_q), .out(RS1), .gate(decoder_3_out19[32]));
  Transistor #(.\type ("n"), .width(32)) transistor_34 (.in(x20_q), .out(RS2), .gate(decoder_3_out20[33]));
  Register #(.width(32)) x19 (.D(RD), .en(decoder_3_out19[34]), .clk(CLK), .Q(x19_q), .clr(RST));
  Transistor #(.\type ("n"), .width(32)) transistor_35 (.in(x27_q), .out(RS1), .gate(decoder_3_out27[32]));
  Transistor #(.\type ("n"), .width(32)) transistor_36 (.in(x28_q), .out(RS2), .gate(decoder_3_out28[33]));
  Register #(.width(32)) x27 (.D(RD), .en(decoder_3_out27[34]), .clk(CLK), .Q(x27_q), .clr(RST));
  Transistor #(.\type ("n"), .width(32)) transistor_37 (.in(x2_q), .out(RS1), .gate(decoder_3_out2[32]));
  Transistor #(.\type ("n"), .width(32)) transistor_38 (.in(x3_q), .out(RS2), .gate(decoder_3_out3[33]));
  Register #(.width(32)) x2 (.D(RD), .en(decoder_3_out2[34]), .clk(CLK), .Q(x2_q), .clr(RST));
  Transistor #(.\type ("n"), .width(32)) transistor_39 (.in(x10_q), .out(RS1), .gate(decoder_3_out10[32]));
  Transistor #(.\type ("n"), .width(32)) transistor_40 (.in(x11_q), .out(RS2), .gate(decoder_3_out11[33]));
  Register #(.width(32)) x10 (.D(RD), .en(decoder_3_out10[34]), .clk(CLK), .Q(x10_q), .clr(RST));
  Transistor #(.\type ("n"), .width(32)) transistor_41 (.in(x18_q), .out(RS1), .gate(decoder_3_out18[32]));
  Transistor #(.\type ("n"), .width(32)) transistor_42 (.in(x19_q), .out(RS2), .gate(decoder_3_out19[33]));
  Register #(.width(32)) x18 (.D(RD), .en(decoder_3_out18[34]), .clk(CLK), .Q(x18_q), .clr(RST));
  Transistor #(.\type ("n"), .width(32)) transistor_43 (.in(x26_q), .out(RS1), .gate(decoder_3_out26[32]));
  Transistor #(.\type ("n"), .width(32)) transistor_44 (.in(x27_q), .out(RS2), .gate(decoder_3_out27[33]));
  Register #(.width(32)) x26 (.D(RD), .en(decoder_3_out26[34]), .clk(CLK), .Q(x26_q), .clr(RST));
  Transistor #(.\type ("n"), .width(32)) transistor_45 (.in(x1_q), .out(RS1), .gate(decoder_3_out1[32]));
  Transistor #(.\type ("n"), .width(32)) transistor_46 (.in(x2_q), .out(RS2), .gate(decoder_3_out2[33]));
  Register #(.width(32)) x1 (.D(RD), .en(decoder_3_out1[34]), .clk(CLK), .Q(x1_q), .clr(RST));
  Transistor #(.\type ("n"), .width(32)) transistor_47 (.in(x9_q), .out(RS1), .gate(decoder_3_out9[32]));
  Transistor #(.\type ("n"), .width(32)) transistor_48 (.in(x10_q), .out(RS2), .gate(decoder_3_out10[33]));
  Register #(.width(32)) x9 (.D(RD), .en(decoder_3_out9[34]), .clk(CLK), .Q(x9_q), .clr(RST));
  Transistor #(.\type ("n"), .width(32)) transistor_49 (.in(x17_q), .out(RS1), .gate(decoder_3_out17[32]));
  Transistor #(.\type ("n"), .width(32)) transistor_50 (.in(x18_q), .out(RS2), .gate(decoder_3_out18[33]));
  Register #(.width(32)) x17 (.D(RD), .en(decoder_3_out17[34]), .clk(CLK), .Q(x17_q), .clr(RST));
  Transistor #(.\type ("n"), .width(32)) transistor_51 (.in(x25_q), .out(RS1), .gate(decoder_3_out25[32]));
  Transistor #(.\type ("n"), .width(32)) transistor_52 (.in(x26_q), .out(RS2), .gate(decoder_3_out26[33]));
  Register #(.width(32)) x25 (.D(RD), .en(decoder_3_out25[34]), .clk(CLK), .Q(x25_q), .clr(RST));
  Transistor #(.\type ("n"), .width(32)) transistor_53 (.in(x1_q), .out(RS2), .gate(decoder_3_out1[33]));
  assign RS1 = decoder_3_out0[32] ? {32{1'b0}} : 32'bz;  // Controlled_Buffer controlled_buffer_1
  Transistor #(.\type ("n"), .width(32)) transistor_54 (.in(x8_q), .out(RS1), .gate(decoder_3_out8[32]));
  Transistor #(.\type ("n"), .width(32)) transistor_55 (.in(x9_q), .out(RS2), .gate(decoder_3_out9[33]));
  Register #(.width(32)) x8 (.D(RD), .en(decoder_3_out8[34]), .clk(CLK), .Q(x8_q), .clr(RST));
  Transistor #(.\type ("n"), .width(32)) transistor_56 (.in(x16_q), .out(RS1), .gate(decoder_3_out16[32]));
  Transistor #(.\type ("n"), .width(32)) transistor_57 (.in(x17_q), .out(RS2), .gate(decoder_3_out17[33]));
  Register #(.width(32)) x16 (.D(RD), .en(decoder_3_out16[34]), .clk(CLK), .Q(x16_q), .clr(RST));
  Transistor #(.\type ("n"), .width(32)) transistor_58 (.in(x24_q), .out(RS1), .gate(decoder_3_out24[32]));
  Transistor #(.\type ("n"), .width(32)) transistor_59 (.in(x25_q), .out(RS2), .gate(decoder_3_out25[33]));
  Register #(.width(32)) x24 (.D(RD), .en(decoder_3_out24[34]), .clk(CLK), .Q(x24_q), .clr(RST));
  assign RS2 = decoder_3_out0[33] ? {32{1'b0}} : 32'bz;  // Controlled_Buffer controlled_buffer_2
  Transistor #(.\type ("n"), .width(32)) transistor_60 (.in(x8_q), .out(RS2), .gate(decoder_3_out8[33]));
  Transistor #(.\type ("n"), .width(32)) transistor_61 (.in(x16_q), .out(RS2), .gate(decoder_3_out16[33]));
  Transistor #(.\type ("n"), .width(32)) transistor_62 (.in(x24_q), .out(RS2), .gate(decoder_3_out24[33]));
  Decoder #(.select(5)) decoder_1 (
    .out0(decoder_3_out0[32]), .out1(decoder_3_out1[32]), .out2(decoder_3_out2[32]),
    .out3(decoder_3_out3[32]), .out4(decoder_3_out4[32]), .out5(decoder_3_out5[32]),
    .out6(decoder_3_out6[32]), .out7(decoder_3_out7[32]), .out8(decoder_3_out8[32]),
    .out9(decoder_3_out9[32]), .out10(decoder_3_out10[32]), .out11(decoder_3_out11[32]),
    .out12(decoder_3_out12[32]), .out13(decoder_3_out13[32]), .out14(decoder_3_out14[32]),
    .out15(decoder_3_out15[32]), .out16(decoder_3_out16[32]), .out17(decoder_3_out17[32]),
    .out18(decoder_3_out18[32]), .out19(decoder_3_out19[32]), .out20(decoder_3_out20[32]),
    .out21(decoder_3_out21[32]), .out22(decoder_3_out22[32]), .out23(decoder_3_out23[32]),
    .out24(decoder_3_out24[32]), .out25(decoder_3_out25[32]), .out26(decoder_3_out26[32]),
    .out27(decoder_3_out27[32]), .out28(decoder_3_out28[32]), .out29(decoder_3_out29[32]),
    .out30(decoder_3_out30[32]), .out31(decoder_3_out31[32]), .sel(RS1S), .en(pull_resistor_1_node));
  Pull_Resistor #(.pull(1)) pull_resistor_1 (.node(pull_resistor_1_node));
  Decoder #(.select(5)) decoder_2 (
    .out0(decoder_3_out0[33]), .out1(decoder_3_out1[33]), .out2(decoder_3_out2[33]),
    .out3(decoder_3_out3[33]), .out4(decoder_3_out4[33]), .out5(decoder_3_out5[33]),
    .out6(decoder_3_out6[33]), .out7(decoder_3_out7[33]), .out8(decoder_3_out8[33]),
    .out9(decoder_3_out9[33]), .out10(decoder_3_out10[33]), .out11(decoder_3_out11[33]),
    .out12(decoder_3_out12[33]), .out13(decoder_3_out13[33]), .out14(decoder_3_out14[33]),
    .out15(decoder_3_out15[33]), .out16(decoder_3_out16[33]), .out17(decoder_3_out17[33]),
    .out18(decoder_3_out18[33]), .out19(decoder_3_out19[33]), .out20(decoder_3_out20[33]),
    .out21(decoder_3_out21[33]), .out22(decoder_3_out22[33]), .out23(decoder_3_out23[33]),
    .out24(decoder_3_out24[33]), .out25(decoder_3_out25[33]), .out26(decoder_3_out26[33]),
    .out27(decoder_3_out27[33]), .out28(decoder_3_out28[33]), .out29(decoder_3_out29[33]),
    .out30(decoder_3_out30[33]), .out31(decoder_3_out31[33]), .sel(RS2S), .en(pull_resistor_4_node));
  Pull_Resistor pull_resistor_2 (.node(RS1S));
  Pull_Resistor pull_resistor_3 (.node(RS2S));
  Pull_Resistor #(.pull(1)) pull_resistor_4 (.node(pull_resistor_4_node));
  Pull_Resistor #(.pull(1)) pull_resistor_5 (.node(pull_resistor_5_node));
  Decoder #(.select(5)) decoder_3 (
    .out0(decoder_3_out0[34]), .out1(decoder_3_out1[34]), .out2(decoder_3_out2[34]),
    .out3(decoder_3_out3[34]), .out4(decoder_3_out4[34]), .out5(decoder_3_out5[34]),
    .out6(decoder_3_out6[34]), .out7(decoder_3_out7[34]), .out8(decoder_3_out8[34]),
    .out9(decoder_3_out9[34]), .out10(decoder_3_out10[34]), .out11(decoder_3_out11[34]),
    .out12(decoder_3_out12[34]), .out13(decoder_3_out13[34]), .out14(decoder_3_out14[34]),
    .out15(decoder_3_out15[34]), .out16(decoder_3_out16[34]), .out17(decoder_3_out17[34]),
    .out18(decoder_3_out18[34]), .out19(decoder_3_out19[34]), .out20(decoder_3_out20[34]),
    .out21(decoder_3_out21[34]), .out22(decoder_3_out22[34]), .out23(decoder_3_out23[34]),
    .out24(decoder_3_out24[34]), .out25(decoder_3_out25[34]), .out26(decoder_3_out26[34]),
    .out27(decoder_3_out27[34]), .out28(decoder_3_out28[34]), .out29(decoder_3_out29[34]),
    .out30(decoder_3_out30[34]), .out31(decoder_3_out31[34]), .sel(RDS), .en(pull_resistor_5_node));
  Pull_Resistor pull_resistor_6 (.node(RDS));
  Decoder #(.select(5)) decoder_4 (
    .out0(RST), .out1(RST), .out2(RST), .out3(RST), .out4(RST), .out5(RST), .out6(RST), .out7(RST),
    .out8(RST), .out9(RST), .out10(RST), .out11(RST), .out12(RST), .out13(RST), .out14(RST), .out15(RST),
    .out16(RST), .out17(RST), .out18(RST), .out19(RST), .out20(RST), .out21(RST), .out22(RST), .out23(RST),
    .out24(RST), .out25(RST), .out26(RST), .out27(RST), .out28(RST), .out29(RST), .out30(RST), .out31(RST));  // open: sel, en

  // Notes on the sheet:
  //   RS1: pull=down
  //   RS2: pull=down
  //   RD: pull=up
  //   RS1S: pull=down
  //   RST: pull=down
  //   RS2S: pull=down
  //   RDS: pull=down
  //   x0
  //   rs1 decoder
  //   rs2 decoder
  //   rd decoder
endmodule

module instruction_decoder (
  input  [31:0] instr,
  output invalid,
  output [5:0] instr_type,
  output [6:0] opcode,
  output [19:0] imm,
  output [6:0] funct7,
  output [2:0] funct3,
  output [4:0] rd,
  output [4:0] rs2,
  output [4:0] rs1
);

  wire [2:0] Data_decoder_out;

  PLA #(.in_width(32), .out_width(3), .\table ("0x00000xxxxxxxxxx000xxxxx0110011 001 # ADD SUB\n0000000xxxxxxxxxx001xxxxx0110011 001 # SLL\n0000000xxxxxxxxxx01xxxxxx0110011 001 # SLT SLTU\n0000000xxxxxxxxxx100xxxxx0110011 001 # XOR\n0x00000xxxxxxxxxx101xxxxx0110011 001 # SRL SRA\n0000000xxxxxxxxxx11xxxxxx0110011 001 # OR AND\nxxxxxxxxxxxxxxxxx000xxxxx1100111 010 # JALR\nxxxxxxxxxxxxxxxxxxx0xxxxx0000011 010 # LB LH LBU LHU\nxxxxxxxxxxxxxxxxx010xxxxx0000011 010 # LW\nxxxxxxxxxxxxxxxxx000xxxxx0010011 010 # ADDI\nxxxxxxxxxxxxxxxxx01xxxxxx0010011 010 # SLTI SLTIU\nxxxxxxxxxxxxxxxxx1x0xxxxx0010011 010 # XORI ORI\nxxxxxxxxxxxxxxxxx111xxxxx0010011 010 # ANDI\n0000000xxxxxxxxxxx01xxxxx0010011 010 # SLLI SRLI\n0100000xxxxxxxxxx101xxxxx0010011 010 # SRAI\nxxxxxxxxxxxxxxxxx0xxxxxxx1100011 011 # SB SH SW\nxxxxxxxxxxxxxxxxxx0xxxxxx1100011 100 # BEQ BNE BLT BGE\nxxxxxxxxxxxxxxxxx11xxxxxx1100011 100 # BLTU BGEU\nxxxxxxxxxxxxxxxxxxxxxxxxx0x10111 101 # LUI AUIPC\nxxxxxxxxxxxxxxxxxxxxxxxxx1101111 110 # JAL")) Data_decoder (
    .in(instr), .out(Data_decoder_out));
  Decoder #(.select(3)) decoder_1 (
    .out0(invalid), .out1(instr_type[0]), .out2(instr_type[1]), .out3(instr_type[2]), .out4(instr_type[3]),
    .out5(instr_type[4]), .out6(instr_type[5]), .sel(Data_decoder_out), .en(1'b1));  // open: out7
  assign {funct7, rs2, rs1, funct3, rd} = instr_type[0] ? instr[31:7] : 25'bz;  // Controlled_Buffer controlled_buffer_1
  assign {imm[11:0], rs1, funct3, rd} = instr_type[1] ? instr[31:7] : 25'bz;  // Controlled_Buffer controlled_buffer_2
  assign {imm[11:5], rs2, rs1, funct3, imm[4:0]} = instr_type[2] ? instr[31:7] : 25'bz;  // Controlled_Buffer controlled_buffer_3
  assign {imm[11], imm[9:4], rs2, rs1, funct3, imm[3:0], imm[10]} = instr_type[3] ? instr[31:7] : 25'bz;  // Controlled_Buffer controlled_buffer_4
  assign {imm, rd} = instr_type[4] ? instr[31:7] : 25'bz;  // Controlled_Buffer controlled_buffer_5
  assign {imm[19], imm[7:0], imm[8], imm[18:9], rd} = instr_type[5] ? instr[31:7] : 25'bz;  // Controlled_Buffer controlled_buffer_6

  assign opcode = instr[6:0];

  // Notes on the sheet:
  //   rs1: pull=down
  //   opcode: pull=down
  //   imm: pull=down
  //   funct7: pull=down
  //   funct3: pull=down
  //   rd: pull=down
  //   rs2: pull=down
  //   U/J imm20
  //   I/B/S imm12
  //   funct7
  //   funct3
endmodule

module doc (
);

  wire controlled_buffer_1_out, controlled_buffer_2_out, controlled_buffer_6_out, controlled_buffer_8_out,
       controlled_buffer_9_out, undriven, undriven_2, undriven_3, undriven_4, undriven_5, undriven_6,
       undriven_7, undriven_8, undriven_9, undriven_10;

  assign controlled_buffer_1_out = undriven_10 ? undriven_7 : 1'bz;  // Controlled_Buffer controlled_buffer_1
  assign controlled_buffer_2_out = undriven_10 ? undriven_4 : 1'bz;  // Controlled_Buffer controlled_buffer_2
  assign controlled_buffer_2_out = undriven_10 ? undriven : 1'bz;  // Controlled_Buffer controlled_buffer_3
  assign controlled_buffer_2_out = undriven_10 ? undriven_2 : 1'bz;  // Controlled_Buffer controlled_buffer_4
  assign controlled_buffer_1_out = undriven_10 ? undriven_3 : 1'bz;  // Controlled_Buffer controlled_buffer_5
  assign controlled_buffer_6_out = undriven_10 ? undriven_8 : 1'bz;  // Controlled_Buffer controlled_buffer_6
  assign controlled_buffer_6_out = undriven_10 ? undriven_9 : 1'bz;  // Controlled_Buffer controlled_buffer_7
  assign controlled_buffer_8_out = undriven_10 ? undriven_5 : 1'bz;  // Controlled_Buffer controlled_buffer_8
  assign controlled_buffer_9_out = undriven_10 ? undriven_6 : 1'bz;  // Controlled_Buffer controlled_buffer_9

  // Notes on the sheet:
  //   R
  //   S
  //   I
  //   Instruction Decode Logic
  //   B
  //   Clock divider (/2)
  //   U
  //   J
  //   stall/resume
  //   Opcode
  //   Valid?
  //   Control Logic
  //   Inputs (from elsewhere on the board)
  //   Instruction
  //   pc
  //   rs1
  //   rs2
  //   rd
  //   Input J/U imm 20
  //   Input S/B/I imm12
  //   function7
  //   function3
  //   Input A-2; Input B-2
  //   Output-1; Output-2
  //   Transform A; Transform B (or zero)
  //   +4
  //   Data I/O Selector
  //   imm12 activated?
  //   Input A-1
  //   Input B-1
  //   Output-1
  //   <- connect as appropriate; switch using clock divider
  //   Input A-2
  //   Input B-2
  //   Output-2
  //   Clock cycle 1: reset
  //   Instruction cycle is 4 clock cycles; load and execute are parallel
  //   Any branch instruction incurs a 6 cycle penalty (4 to load, 2 to decode)
  //   Instructions may perform up to 2 data transforms per instruction cycle
  //   TODO: Instructions longer than 4 cycles? Stall the shift register load to inst?
  //   System is limited by ROM access; faster instruction load? pipeline?
  //   Clock cycle 4n+2: load instruction into shift register
  //   Clock cycle 4n+6: load shift register into decode register
  //   Data transform block
endmodule

module program_counter (
  input  clk,
  input  rst,
  input  read_next,
  input  write_enable,
  output [31:0] instr,
  output [31:0] pc_data
);

  wire and_1_out, and_2_out, and_3_out, comparator_1_eq, comparator_2_eq, counter_1_carry,
       Instruction_loaded_q, Instruction_loaded_qn, not_1_out, not_2_out, not_3_out, or_1_out, or_2_out;
  wire [1:0] counter_1_q;
  wire [7:0] bit_extender_1_out, Init_firmware_data;
  wire [29:0] adder_1_out;
  wire [31:0] controlled_buffer_1_out, PC_q, shift_register_1_p6;
  wire [31:2] controlled_buffer_5_out;

  or or_1 (or_1_out, and_3_out, rst, write_enable);
  assign controlled_buffer_1_out = write_enable ? pc_data : 32'bz;  // Controlled_Buffer controlled_buffer_1
  assign controlled_buffer_1_out = rst ? {32{1'b0}} : 32'bz;  // Controlled_Buffer controlled_buffer_2
  Register #(.width(32)) PC (.D(controlled_buffer_1_out), .en(or_1_out), .clk(clk), .Q(PC_q));  // open: clr
  not not_1 (not_1_out, read_next);
  not not_2 (not_2_out, write_enable);
  and and_1 (and_1_out, read_next, not_2_out);
  and and_2 (and_2_out, not_1_out, not_2_out);
  assign pc_data = and_2_out ? PC_q : 32'bz;  // Controlled_Buffer controlled_buffer_3
  assign pc_data = and_1_out ? {controlled_buffer_5_out, 2'b00} : 32'bz;  // Controlled_Buffer controlled_buffer_4
  or or_2 (or_2_out, rst, write_enable);
  assign controlled_buffer_5_out = Instruction_loaded_q ? adder_1_out : 30'bz;  // Controlled_Buffer controlled_buffer_5
  Adder #(.width(30)) adder_1 (.a(30'h1), .b(PC_q[31:2]), .out(adder_1_out));  // open: cin, cout
  assign controlled_buffer_5_out = Instruction_loaded_qn ? PC_q[31:2] : 30'bz;  // Controlled_Buffer controlled_buffer_6
  assign controlled_buffer_1_out = and_3_out ? {controlled_buffer_5_out, 2'b00} : 32'bz;  // Controlled_Buffer controlled_buffer_7
  Counter #(.max('h3), .width(2)) counter_1 (
    .clr(or_2_out), .load(1'b0), .up(1'b1), .count(1'b1), .clk(clk), .carry(counter_1_carry), .Q(counter_1_q));  // open: D
  S_R_Flip_Flop Instruction_loaded (
    .S(counter_1_carry), .R(1'b0), .clk(clk), .Q(Instruction_loaded_q), .reset(or_2_out),
    .Qn(Instruction_loaded_qn));  // open: preset
  and and_3 (and_3_out, counter_1_carry, Instruction_loaded_q, not_3_out);
  Bit_Extender #(.in_width(32), .out_width(8), .\type ("zero")) bit_extender_1 (
    .in({controlled_buffer_5_out, counter_1_q}), .out(bit_extender_1_out));
  ROM Init_firmware (.addr(bit_extender_1_out), .data(Init_firmware_data));
  Comparator #(.mode("unsigned"), .width(2)) comparator_1 (
    .a(2'b00), .b(counter_1_q), .eq(comparator_1_eq));  // open: gt, lt
  Register #(.width(32)) Instruction (
    .D(shift_register_1_p6), .en(comparator_1_eq), .clk(clk), .Q(instr), .clr(or_2_out));
  // Shift_Register #(.length(4), .width(8)) shift_register_1: pin names not known; wires that end beside it: or_2_out, 1'b0, 1'b1, clk, Init_firmware_data, shift_register_1_p6[7:0], shift_register_1_p6[15:8], shift_register_1_p6[23:16], shift_register_1_p6[31:24]
  not not_3 (not_3_out, comparator_2_eq);
  Comparator #(.mode("unsigned"), .width(32)) comparator_2 (
    .a({32{1'b0}}), .b(instr), .eq(comparator_2_eq));  // open: gt, lt

  // Notes on the sheet:
  //   pc_data: pull=down
  //   init-vector
  //   programs load 8 bits at a time, but data/address width is 32 bits = 4 cycles per instruction
  //   WARNING: PC increments 1 cycle before updating instruction register!
  //   contents of Init_firmware (hex, n*v repeats v):
  //   0 0 10 b7 0 0 81 67 18 ba 58 37 10 2 48 37 72 e6 e2 37 5a 7e f4 17 58 73 e7 37 7c 2c c6 37 d6 8c 73
  //   37 b9 c9 c2 37 7e 22 94 37 43 42 d9 37 1c 6d bd 37 9c 68 5b 37 0 e 97 37 6e 76 97 37 9c 91 57 37 30
  //   50 d 37 bf 21 e8 37 4e c8 7 37 3 77 3f 37 e7 8a 94 37 3 9c 68 37 3d 26 3e 27 d2 83 1c 85 e4 2e 26 5d
  //   da 52 b6 24 3f 9f 90 8f 88 8 e8 8a 6c 94 48 f5 8f 4a a0 db d6 c5 ca 68 5a 3d f1 95 bb 81 75 2e 24 c1
  //   4a 98 90 9a a3 74 90 db 76 5f f7 35 f7 4e 22 ce 6d 6d a 90 d8 83 d6 2f 6f f8 14 94 75 65 21 38 46 85
  //   8a 7c a2 62 30 dc 29 17 e6 e9 c c6 cc 37 2c e6 5e 8d 79 3a 4f a4 cf 63 bd e4 2 56 57 2b d3 75 a0 97
  //   51 68 71 de c 77 37 d8 72 2a a6 92 b6 74 17 50 c8 d0 2b 87 5a 85 3c 6d 63 2c 8d b9 34 12 4b 51 ef 1f
  //   9a 9 ae c4 38 33 42 d7 fc f1 54 d5 9 e5 a4 81
endmodule
